# Fritzing sketch circuito (saved by Fritzing 0.8.5b)
breadboards: 1

parts:
  Raspberry_Pi_B_rev1 = Raspberry Pi B rev1
  LED1 = LED - 5mm [color="Red (633nm)" package="5 mm [THT]"]
  LED2 = LED - 5mm [color="Green (565nm)" package="5 mm [THT]"]
  U1 = LCD-16X2 [package=lcd-16x2]
  Parte1 = RFID USB Reader
  U2 = MLX90614 [package=to-39]
  R1 = Resistor [tolerance=±5% resistance=1k package=THT]
  R2 = Resistor [tolerance=±5% resistance=220 package=THT]
  LED3 = LED - 5mm [color="Yellow (592nm)" package="5 mm [THT]"]

nets:
  3V3: Raspberry_Pi_B_rev1.3V3, Parte1.VCC
  N1: Raspberry_Pi_B_rev1.GPIO_0, U1.DB2
  N2: Raspberry_Pi_B_rev1.GPIO_1, U1.DB0
  GND: Raspberry_Pi_B_rev1.GND, LED1.cathode, LED2.cathode, Parte1.TX-O, U2.VSS, R1.Pin_0, LED3.cathode
  N3: Raspberry_Pi_B_rev1.GPIO_23, U2.SCL_VZ
  N4: Raspberry_Pi_B_rev1.GPIO_17, LED1.anode
  N5: Raspberry_Pi_B_rev1.GPIO_21, LED2.anode
  N6: Raspberry_Pi_B_rev1.GPIO_22, LED3.anode
  N7: Raspberry_Pi_B_rev1.GPIO_24, R1.Pin_1, R2.Pin_0
  N8: Raspberry_Pi_B_rev1.GPIO_10, Parte1.ANT2
  N9: Raspberry_Pi_B_rev1.GPIO_9, Parte1.ANT1
  N10: Raspberry_Pi_B_rev1.GPIO_25, Parte1.GND
  N11: Raspberry_Pi_B_rev1.GPIO_11, Parte1.CP
  N12: Raspberry_Pi_B_rev1.GPIO_8, Parte1.GNDT
  N13: U1.DB5, U2.VDD
  N14: U2.PWM_SDA, R2.Pin_1

notes:
  Sensor de ultrasonidos:
  Negro - ground
  Rojo - power
  Morado - Trigger
  Amarillo - Echo
  Lector RFID:
  Rojo - power
  Negro - ground
